// Logisim project hw1-q4-moregates.circ as structural Verilog: 1 circuit, main circuit main
module main (
  input  x1,
  input  in_2,
  input  x2,
  input  x3,
  input  x4
);

  wire and_1_out, and_2_out, and_3_out, and_4_out, and_5_out, and_6_out, and_7_out, not_1_out, not_2_out,
       not_3_out, or_1_out, or_2_out, or_3_out, xor_1_out;

  not not_1 (not_1_out, x2);
  not not_2 (not_2_out, x3);
  not not_3 (not_3_out, x4);
  xor xor_1 (xor_1_out, in_2, x2);
  and and_1 (and_1_out, x1, xor_1_out);
  and and_2 (and_2_out, not_2_out, in_2, not_1_out);
  and and_3 (and_3_out, x1, in_2, not_2_out);
  and and_4 (and_4_out, x2, x1, x3);
  and and_5 (and_5_out, x1, not_2_out, not_1_out);
  or or_1 (or_1_out, and_1_out, and_2_out, and_3_out);
  or or_2 (or_2_out, and_3_out, and_4_out, and_5_out);
  and and_6 (and_6_out, or_1_out, not_3_out);
  and and_7 (and_7_out, x4, or_2_out);
  LED led_1 (.in(or_3_out));
  or or_3 (or_3_out, and_6_out, and_7_out);

  // Notes on the sheet:
  //   x0
  //   f
endmodule
