// Logisim project hw5_datapath.circ as structural Verilog: 3 circuits, main circuit main
module main (
  input  [2:0] sel,
  input  s1,
  input  s2,
  input  cs,
  input  r,
  input  lda,
  input  ldb,
  input  s3,
  input  s4,
  input  c0,
  input  [3:0] addr,
  output [7:0] out_12
);

  wire alu_1_out_6, alu_1_out_7, alu_1_out_8, clock_1_out, not_1_out;
  wire [7:0] multiplexer_1_out, multiplexer_2_out, multiplexer_3_out, multiplexer_4_out, ram_1_data, RegA_q,
       RegB_q;

  Multiplexer #(.width(8), .disabled(0), .enable("false")) multiplexer_1 (
    .in0(RegA_q), .in1(RegB_q), .out(multiplexer_1_out), .sel(s1));
  Clock clock_1 (.out(clock_1_out));
  Multiplexer #(.width(8), .disabled(0), .enable("false")) multiplexer_2 (
    .in0(ram_1_data), .in1(out_12), .out(multiplexer_2_out), .sel(s2));
  not not_1 (not_1_out, r);
  RAM #(.addrWidth(4), .bus("separate")) ram_1 (
    .addr(addr), .din(multiplexer_1_out), .data(ram_1_data), .str(not_1_out), .sel(cs), .clk(clock_1_out),
    .ld(r));  // open: clr
  Register RegA (.D(multiplexer_2_out), .en(lda), .Q(RegA_q), .clk(clock_1_out));  // open: clr
  Register RegB (.D(multiplexer_2_out), .en(ldb), .Q(RegB_q), .clk(clock_1_out));  // open: clr
  Multiplexer #(.width(8), .disabled(0), .enable("false")) multiplexer_3 (
    .in0(ram_1_data), .in1(RegA_q), .out(multiplexer_3_out), .sel(s3));
  Multiplexer #(.width(8), .disabled(0), .enable("false")) multiplexer_4 (
    .in0(ram_1_data), .in1(RegB_q), .out(multiplexer_4_out), .sel(s4));
  ALU alu_1 (
    .sel(sel), .op1(multiplexer_3_out), .op2(multiplexer_4_out), .res(out_12), .c0(c0), .out_6(alu_1_out_6),
    .out_7(alu_1_out_7), .out_8(alu_1_out_8));

  // Notes on the sheet:
  //   RAM
endmodule

module ALU (
  input  [2:0] sel,
  input  c0,
  input  [7:0] op1,
  input  [7:0] op2,
  output [7:0] res,
  output out_6,
  output out_7,
  output out_8
);

  wire adder_1_cout, and_2_out, and_3_out, nor_1_out, or_2_out;
  wire [7:0] adder_1_out, and_1_out, multiplexer_1_out, multiplexer_2_out, multiplexer_3_out, optnot8_1_out,
       or_1_out;

  Multiplexer #(.width(8), .disabled(0), .enable("false")) multiplexer_1 (
    .in0(op1), .in1({8{1'b0}}), .out(multiplexer_1_out), .sel(sel[2]));
  assign and_1_out = op2 & op1;  // AND_Gate and_1, 8 bits wide
  assign or_1_out = op1 | op2;  // OR_Gate or_1, 8 bits wide
  Comparator comparator_1 (.a(op1), .b(op2), .gt(out_6), .eq(out_7), .lt(out_8));
  optNOT8 optnot8_1 (.in(op2), .out(optnot8_1_out), .inv(sel[1]));
  Multiplexer #(.width(8), .disabled(0), .enable("false")) multiplexer_2 (
    .in0(and_1_out), .in1(or_1_out), .out(multiplexer_2_out), .sel(sel[2]));
  and and_2 (and_2_out, ~sel[0], ~sel[1], sel[2]);  // AND_Gate
  nor nor_1 (nor_1_out, sel[0], sel[1], sel[2]);
  and and_3 (and_3_out, sel[0], sel[1]);
  or or_2 (or_2_out, and_2_out, nor_1_out);
  Multiplexer #(.width(8), .disabled(0), .enable("false")) multiplexer_3 (
    .in0(optnot8_1_out), .in1({8{1'b0}}), .out(multiplexer_3_out), .sel(or_2_out));
  Adder adder_1 (.a(multiplexer_1_out), .b(multiplexer_3_out), .out(adder_1_out), .cin(c0), .cout(adder_1_cout));
  Multiplexer #(.width(8), .disabled(0), .enable("false")) multiplexer_4 (
    .in0(adder_1_out), .in1(multiplexer_2_out), .out(res), .sel(and_3_out));
endmodule

module optNOT8 (
  input  inv,
  input  [7:0] in,
  output [7:0] out
);

  xor xor_1 (out[7], inv, in[7]);
  xor xor_2 (out[6], inv, in[6]);
  xor xor_3 (out[5], inv, in[5]);
  xor xor_4 (out[4], inv, in[4]);
  xor xor_5 (out[3], inv, in[3]);
  xor xor_6 (out[2], inv, in[2]);
  xor xor_7 (out[1], inv, in[1]);
  xor xor_8 (out[0], inv, in[0]);
endmodule
