// Logisim project hw5-q3.circ as structural Verilog: 1 circuit, main circuit main
module main (
  output [4:0] Output,
  output [2:0] Clock_check
);

  wire and_1_out, clock_1_out, d_ff_1_q, d_ff_2_q;

  Clock clock_1 (.out(clock_1_out));
  D_Flip_Flop d_ff_1 (
    .clk(clock_1_out), .D(Clock_check[0]), .Q(d_ff_1_q), .Qn(Clock_check[0]), .preset(and_1_out));  // open: en, reset
  and and_1 (and_1_out, Clock_check[2], Clock_check[1]);
  D_Flip_Flop d_ff_2 (
    .clk(d_ff_1_q), .D(Clock_check[1]), .Q(d_ff_2_q), .Qn(Clock_check[1]), .preset(and_1_out));  // open: en, reset
  D_Flip_Flop d_ff_3 (
    .clk(d_ff_2_q), .D(Clock_check[2]), .Qn(Clock_check[2]), .preset(and_1_out));  // open: Q, en, reset
  Multiplexer #(.select(3), .width(5), .enable("false")) multiplexer_1 (
    .in0(5'b10000), .in1(5'b01101), .in2(5'b11011), .in3(5'b10001), .in4(5'b01100), .in5(5'b11010),
    .out(Output), .sel(Clock_check));  // open: in6, in7
endmodule
