// Logisim project hw1-q2e.circ as structural Verilog: 1 circuit, main circuit main
module main (
  input  a,
  input  b,
  input  c,
  input  d,
  output E
);

  wire and_1_out, nor_1_out, or_1_out, or_2_out;

  and and_1 (and_1_out, ~a, b);  // AND_Gate
  nor nor_1 (nor_1_out, c, d);
  or or_1 (or_1_out, d, c, ~b, a);  // OR_Gate
  or or_2 (or_2_out, and_1_out, nor_1_out);
  nand nand_1 (E, or_2_out, or_1_out);
endmodule
