// Logisim project hw1-q2f.circ as structural Verilog: 1 circuit, main circuit main
module main (
  input  a,
  input  b,
  input  c,
  input  d,
  output F
);

  wire and_1_out, nor_1_out, xnor_1_out, xor_1_out;

  xor xor_1 (xor_1_out, c, d);
  and and_1 (and_1_out, ~b, a);  // AND_Gate
  xnor xnor_1 (xnor_1_out, a, b);
  nor nor_1 (nor_1_out, d, c);
  or or_1 (F, xor_1_out, xnor_1_out, nor_1_out, and_1_out);
endmodule
