// Logisim project hw1-q4.circ as structural Verilog: 1 circuit, main circuit main
module main (
  input  x1,
  input  in_2,
  input  x2,
  input  x3,
  input  x4
);

  wire and_1_out, and_2_out, and_3_out, and_4_out, and_5_out, and_6_out, or_1_out, or_2_out;

  and and_1 (and_1_out, x1, ~in_2, x2, x3);  // AND_Gate
  and and_2 (and_2_out, x1, x2, ~x3, ~x4);  // AND_Gate
  and and_3 (and_3_out, in_2, ~x3, ~x4, ~x2);  // AND_Gate
  and and_4 (and_4_out, x1, in_2, ~x2, ~x4);  // AND_Gate
  and and_5 (and_5_out, x1, ~x2, ~x3, x4);  // AND_Gate
  and and_6 (and_6_out, x1, in_2, x2, x4);
  or or_1 (or_1_out, and_1_out, and_2_out, and_3_out, and_4_out, and_5_out);
  LED led_1 (.in(or_2_out));
  or or_2 (or_2_out, or_1_out, and_6_out);

  // Notes on the sheet:
  //   x0
  //   z
endmodule
