// Logisim project hw3-q6.circ as structural Verilog: 5 circuits, main circuit main
module main (
  input  in_1,
  input  d,
  input  ld,
  output out_4,
  output out_5
);

  wire and_1_out, clock_1_out, clock_2_out, xor_1_out;

  Clock clock_1 (.out(clock_1_out));
  xor xor_1 (xor_1_out, out_5, d);
  Clock clock_2 (.out(clock_2_out));
  and and_1 (and_1_out, xor_1_out, ld);
  T_flipflop t_flipflop_1 (
    .in_1(in_1), .in_3(1'b0), .in_4(1'b1), .in_5(1'b0), .out_6(out_4), .in_2(clock_2_out));  // open: out_7
  T_Flip_Flop t_ff_1 (.clk(clock_1_out), .T(and_1_out), .Q(out_5));  // open: Qn, preset, reset, en
endmodule

module T_flipflop (
  input  in_1,
  input  in_2,
  input  in_3,
  input  in_4,
  input  in_5,
  output out_6,
  output out_7
);

  J_K_Flip_Flop j_k_ff_1 (
    .J(in_1), .clk(in_2), .K(in_1), .Q(out_6), .Qn(out_7), .preset(in_3), .en(in_4), .reset(in_5));
endmodule

module _1_bit_register (
  input  clk,
  input  d,
  input  ld,
  output out_4
);

  wire and_1_out, xor_1_out;

  xor xor_1 (xor_1_out, out_4, d);
  and and_1 (and_1_out, xor_1_out, ld);
  T_flipflop t_flipflop_1 (
    .in_1(and_1_out), .in_3(1'b0), .in_4(1'b1), .in_5(1'b0), .out_6(out_4), .in_2(clk));  // open: out_7
endmodule

module _4_bit_register (
  input  in_1,
  input  [3:0] in_2,
  input  in_3,
  output [3:0] out_4
);

  _1_bit_register u_1_bit_register_1 (.clk(in_3), .d(in_2[0]), .ld(in_1), .out_4(out_4[0]));
  _1_bit_register u_1_bit_register_2 (.clk(in_3), .d(in_2[1]), .ld(in_1), .out_4(out_4[1]));
  _1_bit_register u_1_bit_register_3 (.clk(in_3), .d(in_2[2]), .ld(in_1), .out_4(out_4[2]));
  _1_bit_register u_1_bit_register_4 (.clk(in_3), .d(in_2[3]), .ld(in_1), .out_4(out_4[3]));
endmodule

module PC (
  input  [3:0] addr_in,
  input  ld,
  input  up,
  input  clk,
  input  clr,
  output [3:0] out_6
);

  wire or_1_out;
  wire [3:0] adder_1_out, multiplexer_1_out, n4_bit_register_1_out_4;

  Adder #(.width(4)) adder_1 (.a(n4_bit_register_1_out_4), .b(4'b0001), .out(adder_1_out));  // open: cin, cout
  Multiplexer #(.width(4), .disabled(0), .enable("false")) multiplexer_1 (
    .in0(adder_1_out), .in1(addr_in), .out(multiplexer_1_out), .sel(ld));
  or or_1 (or_1_out, ld, up);
  _4_bit_register u_4_bit_register_1 (
    .in_1(or_1_out), .in_2(multiplexer_1_out), .in_3(clk), .out_4(n4_bit_register_1_out_4));
  Multiplexer #(.width(4), .disabled(0), .enable("false")) multiplexer_2 (
    .in0(n4_bit_register_1_out_4), .in1(4'b0000), .out(out_6), .sel(clr));
endmodule
