// Logisim project binary-count-starter.circ as structural Verilog: 1 circuit, main circuit main
module main (
  input  \input ,
  output accepting
);

  wire clock_out, multiplexer_1_out, multiplexer_2_out, not_1_out, sb_0_q, sb_1_q, xor_1_out;

  not not_1 (not_1_out, sb_0_q);
  xor xor_1 (xor_1_out, sb_0_q, sb_1_q);
  Multiplexer #(.enable("false")) multiplexer_1 (.in0(sb_0_q), .in1(not_1_out), .out(multiplexer_1_out), .sel(\input ));
  Multiplexer #(.enable("false")) multiplexer_2 (.in0(sb_1_q), .in1(xor_1_out), .out(multiplexer_2_out), .sel(\input ));
  Clock clock (.out(clock_out));
  D_Flip_Flop sb_0 (.clk(clock_out), .D(multiplexer_1_out), .Q(sb_0_q));  // open: Qn, preset, en, reset
  D_Flip_Flop sb_1 (.clk(clock_out), .D(multiplexer_2_out), .Q(sb_1_q));  // open: Qn, preset, en, reset
  and and_1 (accepting, ~sb_0_q, ~sb_1_q);  // AND_Gate
endmodule
