// Logisim project turnstile-starter.circ as structural Verilog: 1 circuit, main circuit main
module main (
  input  \input ,
  output \output 
);

  wire clock_out;

  Clock clock (.out(clock_out));
  D_Flip_Flop state_bit (.clk(clock_out), .D(\input ), .Q(\output ));  // open: Qn, preset, en, reset

  // Notes on the sheet:
  //   next_state_bit
endmodule
