// Logisim project traffic-light-starter.circ as structural Verilog: 2 circuits, main circuit main
module main (
  input  p,
  input  t,
  output accepting
);

  wire clock_out, clock_verify_clock_out, multiplexer_1_out, multiplexer_2_out, multiplexer_3_out;
  wire [2:0] sb_0_q;

  Clock clock (.out(clock_out));
  Multiplexer #(.select(3)) multiplexer_1 (
    .in0(p), .in1(p), .in2(t), .in3(p), .in4(t), .in5(p), .in6(1'b0), .out(multiplexer_1_out), .sel(sb_0_q));  // open: in7, en
  Multiplexer #(.select(3)) multiplexer_2 (
    .in0(1'b0), .in1(t), .in2(t), .in3(1'b0), .in4(1'b0), .in5(t), .in6(p), .out(multiplexer_2_out),
    .sel(sb_0_q));  // open: in7, en
  Multiplexer #(.select(3)) multiplexer_3 (
    .in0(1'b0), .in1(1'b0), .in2(p), .in3(p), .in4(1'b1), .in5(1'b1), .in6(p), .out(multiplexer_3_out),
    .sel(sb_0_q));  // open: in7, en
  input_verifier clock_verify (.clock_in(clock_out), .p(t), .t(p), .clock_out(clock_verify_clock_out));
  D_Flip_Flop sb_0 (.clk(clock_verify_clock_out), .D(multiplexer_1_out), .Q(sb_0_q[0]));  // open: Qn, preset, en, reset
  D_Flip_Flop sb_1 (.clk(clock_verify_clock_out), .D(multiplexer_2_out), .Q(sb_0_q[1]));  // open: Qn, preset, en, reset
  D_Flip_Flop sb_2 (.clk(clock_verify_clock_out), .D(multiplexer_3_out), .Q(sb_0_q[2]));  // open: Qn, preset, en, reset
  nor nor_1 (accepting, sb_0_q[0], sb_0_q[1], sb_0_q[2]);
endmodule

module input_verifier (
  input  clock_in,
  input  p,
  input  t,
  output clock_out
);

  wire xor_1_out;

  xor xor_1 (xor_1_out, p, t);
  and and_1 (clock_out, clock_in, xor_1_out);
endmodule
